// Logisim project SDMAC.circ as structural Verilog: 12 circuits, main circuit FIFO
module FIFO (
  input  INC_FIFO,
  input  DEC_FIFO,
  input  INC_NI,
  input  [31:0] ID,
  input  INC_NO,
  input  INC_BO,
  input  nRST,
  input  MID25,
  input  ACR_WR,
  input  h_0C,
  input  LHW,
  input  nLB,
  input  LLW,
  output FIFO_EMPTY,
  output FIFO_FULL,
  output [31:0] OD,
  output BOEQ0,
  output BOEQ3
);

  wire FIFO_BytePointer_1_bo0, FIFO_BytePointer_1_bo1, FIFO_WriteStrobes_1_llws, FIFO_WriteStrobes_1_lmws,
       FIFO_WriteStrobes_1_umws, FIFO_WriteStrobes_1_uuws;
  wire [7:0] ReadPointer_d, WritePointer_d;

  nor nor_1 (BOEQ0, FIFO_BytePointer_1_bo1, FIFO_BytePointer_1_bo0);
  FIFO_BytePointer FIFO_BytePointer_1 (
    .INCBO(INC_BO), .nRST(nRST), .MID25(MID25), .ACR_WR(ACR_WR), .h_0C(h_0C), .BO0(FIFO_BytePointer_1_bo0),
    .BO1(FIFO_BytePointer_1_bo1));
  // Probe on WritePointer_d
  // Probe on ReadPointer_d
  and and_1 (BOEQ3, FIFO_BytePointer_1_bo1, FIFO_BytePointer_1_bo0);
  FIFO_FullEmptyCounter FIFO_FullEmptyCounter_1 (
    .nRST_FIFO(nRST), .INC_FIFO(INC_FIFO), .DEC_FIFO(DEC_FIFO), .FIFO_FULL(FIFO_FULL), .FIFO_EMPTY(FIFO_EMPTY));
  FIFO_NextLocationPointer WritePointer (.Inc(INC_NI), .nRST(nRST), .D(WritePointer_d));
  FIFO_NextLocationPointer ReadPointer (.Inc(INC_NO), .nRST(nRST), .D(ReadPointer_d));
  FIFO_WriteStrobes FIFO_WriteStrobes_1 (
    .BO0(FIFO_BytePointer_1_bo0), .BO1(FIFO_BytePointer_1_bo1), .lhw(LHW), .nlb(nLB), .llw(LLW),
    .LLWS(FIFO_WriteStrobes_1_llws), .LMWS(FIFO_WriteStrobes_1_lmws), .UMWS(FIFO_WriteStrobes_1_umws),
    .UUWS(FIFO_WriteStrobes_1_uuws));
  FIFO_Buffer FIFO_Buffer_1 (
    .NI(WritePointer_d), .NO(ReadPointer_d), .DIN(ID), .LLWS(FIFO_WriteStrobes_1_llws),
    .LMWS(FIFO_WriteStrobes_1_lmws), .UMWS(FIFO_WriteStrobes_1_umws), .UUWS(FIFO_WriteStrobes_1_uuws),
    .DOUT(OD));
endmodule

module FIFO_WriteStrobes (
  input  BO0,
  input  BO1,
  input  lhw,
  input  nlb,
  input  llw,
  output LLWS,
  output LMWS,
  output UMWS,
  output UUWS
);

  wire nor_1_out, nor_2_out, nor_3_out, nor_4_out, nor_5_out, nor_6_out, nor_7_out, nor_8_out, not_1_out,
       not_2_out;

  not not_1 (not_1_out, BO0);
  not not_2 (not_2_out, BO1);
  nor nor_1 (nor_1_out, not_1_out, BO1, nlb);
  nor nor_2 (nor_2_out, not_2_out, BO0, nlb);
  nor nor_3 (nor_3_out, not_2_out, not_1_out, nlb);
  nor nor_4 (nor_4_out, BO0, BO1, nlb);
  nor nor_5 (nor_5_out, nor_4_out, lhw);
  not not_3 (UUWS, nor_5_out);
  nor nor_6 (nor_6_out, nor_1_out, lhw);
  not not_4 (UMWS, nor_6_out);
  nor nor_7 (nor_7_out, nor_2_out, llw);
  not not_5 (LMWS, nor_7_out);
  nor nor_8 (nor_8_out, nor_3_out, llw);
  not not_6 (LLWS, nor_8_out);
endmodule

module FIFO_BytePointer (
  input  INCBO,
  input  nRST,
  input  MID25,
  input  ACR_WR,
  input  h_0C,
  output BO0,
  output BO1
);

  wire d_ff_1_qn, multiplexer_1_out, not_1_out, not_2_out, not_3_out, not_4_out, or_1_out, xnor_1_out;

  not not_1 (not_1_out, nRST);
  xnor xnor_1 (xnor_1_out, BO1, BO0);
  not not_2 (not_2_out, MID25);
  or or_1 (or_1_out, INCBO, ACR_WR);
  not not_3 (not_3_out, d_ff_1_qn);
  Multiplexer multiplexer_1 (.in0(xnor_1_out), .in1(not_2_out), .out(multiplexer_1_out), .sel(h_0C));
  not not_4 (not_4_out, not_3_out);
  D_Flip_Flop d_ff_1 (.D(not_4_out), .clk(INCBO), .Q(BO0), .Qn(d_ff_1_qn), .preset(1'b0), .reset(not_1_out));
  D_Flip_Flop d_ff_2 (.D(multiplexer_1_out), .clk(or_1_out), .Q(BO1), .preset(1'b0), .reset(1'b0));  // open: Qn
  // Probe on {BO1, BO0}

  // Notes on the sheet:
  //   nRST: initial=0x1
endmodule

module FIFO_NextLocationPointer (
  input  Inc,
  input  nRST,
  output [7:0] D
);

  wire d_ff_1_qn, d_ff_2_qn, nor_1_out, not_1_out, not_2_out, not_3_out, not_4_out, not_5_out, not_6_out,
       not_7_out, xor_1_out, xor_2_out;
  wire [2:0] d_ff_1_q;

  not not_1 (not_1_out, nRST);
  xor xor_1 (xor_1_out, d_ff_1_q[1], d_ff_1_q[0]);
  xor xor_2 (xor_2_out, d_ff_1_q[2], nor_1_out);
  not not_2 (not_2_out, d_ff_1_qn);
  not not_3 (not_3_out, not_4_out);
  not not_4 (not_4_out, xor_1_out);
  not not_5 (not_5_out, xor_2_out);
  not not_6 (not_6_out, not_5_out);
  D_Flip_Flop d_ff_1 (.D(not_7_out), .clk(Inc), .Q(d_ff_1_q[0]), .Qn(d_ff_1_qn), .reset(not_1_out));  // open: preset
  not not_7 (not_7_out, not_2_out);
  D_Flip_Flop d_ff_2 (.D(not_3_out), .clk(Inc), .Q(d_ff_1_q[1]), .Qn(d_ff_2_qn), .reset(not_1_out));  // open: preset
  D_Flip_Flop d_ff_3 (.D(not_6_out), .clk(Inc), .Q(d_ff_1_q[2]), .reset(not_1_out));  // open: Qn, preset
  nor nor_1 (nor_1_out, d_ff_2_qn, d_ff_1_qn);
  Decoder #(.enable("false"), .select(3)) decoder_1 (
    .out0(D[0]), .out1(D[1]), .out2(D[2]), .out3(D[3]), .out4(D[4]), .out5(D[5]), .out6(D[6]), .out7(D[7]),
    .sel(d_ff_1_q));
endmodule

module FIFO_Buffer (
  input  [7:0] NI,
  input  [7:0] NO,
  input  [31:0] DIN,
  input  LLWS,
  input  LMWS,
  input  UMWS,
  input  UUWS,
  output [31:0] DOUT
);

  FIFO_LongWordBuffer FIFO_LongWordBuffer_1 (
    .DIN(DIN), .LLWS(LLWS), .NI(NI[0]), .NO(NO[0]), .LMWS(LMWS), .UMWS(UMWS), .UUWS(UUWS), .DOUT(DOUT));
  FIFO_LongWordBuffer FIFO_LongWordBuffer_2 (
    .DIN(DIN), .LLWS(LLWS), .NI(NI[1]), .NO(NO[1]), .LMWS(LMWS), .UMWS(UMWS), .UUWS(UUWS), .DOUT(DOUT));
  FIFO_LongWordBuffer FIFO_LongWordBuffer_3 (
    .DIN(DIN), .LLWS(LLWS), .NI(NI[2]), .NO(NO[2]), .LMWS(LMWS), .UMWS(UMWS), .UUWS(UUWS), .DOUT(DOUT));
  FIFO_LongWordBuffer FIFO_LongWordBuffer_4 (
    .DIN(DIN), .LLWS(LLWS), .NI(NI[3]), .NO(NO[3]), .LMWS(LMWS), .UMWS(UMWS), .UUWS(UUWS), .DOUT(DOUT));
  FIFO_LongWordBuffer FIFO_LongWordBuffer_5 (
    .DIN(DIN), .LLWS(LLWS), .NI(NI[4]), .NO(NO[4]), .LMWS(LMWS), .UMWS(UMWS), .UUWS(UUWS), .DOUT(DOUT));
  FIFO_LongWordBuffer FIFO_LongWordBuffer_6 (
    .DIN(DIN), .LLWS(LLWS), .NI(NI[5]), .NO(NO[5]), .LMWS(LMWS), .UMWS(UMWS), .UUWS(UUWS), .DOUT(DOUT));
  FIFO_LongWordBuffer FIFO_LongWordBuffer_7 (
    .DIN(DIN), .LLWS(LLWS), .NI(NI[6]), .NO(NO[6]), .LMWS(LMWS), .UMWS(UMWS), .UUWS(UUWS), .DOUT(DOUT));
  FIFO_LongWordBuffer FIFO_LongWordBuffer_8 (
    .DIN(DIN), .LLWS(LLWS), .NI(NI[7]), .NO(NO[7]), .LMWS(LMWS), .UMWS(UMWS), .UUWS(UUWS), .DOUT(DOUT));
endmodule

module FIFO_LongWordBuffer (
  input  [31:0] DIN,
  input  LLWS,
  input  NI,
  input  NO,
  input  LMWS,
  input  UMWS,
  input  UUWS,
  output [31:0] DOUT
);

  wire buffer_1_out, nand_1_out, nand_2_out, nand_3_out, nand_4_out, not_1_out, not_2_out, not_3_out,
       not_4_out;
  wire [7:0] register_1_q, register_2_q, register_3_q, register_4_q;

  nand nand_1 (nand_1_out, LLWS, NI);
  buf buffer_1 (buffer_1_out, NO);
  nand nand_2 (nand_2_out, LMWS, NI);
  nand nand_3 (nand_3_out, UMWS, NI);
  nand nand_4 (nand_4_out, UUWS, NI);
  not not_1 (not_1_out, nand_1_out);
  not not_2 (not_2_out, nand_2_out);
  not not_3 (not_3_out, nand_3_out);
  not not_4 (not_4_out, nand_4_out);
  Register register_1 (.D(DIN[7:0]), .en(not_1_out), .clk(not_1_out), .Q(register_1_q), .clr(1'b0));
  Register register_2 (.D(DIN[15:8]), .en(not_2_out), .clk(not_2_out), .Q(register_2_q), .clr(1'b0));
  Register register_3 (.D(DIN[23:16]), .en(not_3_out), .clk(not_3_out), .Q(register_3_q), .clr(1'b0));
  Register register_4 (.D(DIN[31:24]), .en(not_4_out), .clk(not_4_out), .Q(register_4_q), .clr(1'b0));
  assign DOUT[7:0] = buffer_1_out ? register_1_q : 8'bz;  // Controlled_Buffer controlled_buffer_1
  assign DOUT[15:8] = buffer_1_out ? register_2_q : 8'bz;  // Controlled_Buffer controlled_buffer_2
  assign DOUT[23:16] = buffer_1_out ? register_3_q : 8'bz;  // Controlled_Buffer controlled_buffer_3
  assign DOUT[31:24] = buffer_1_out ? register_4_q : 8'bz;  // Controlled_Buffer controlled_buffer_4

  // Notes on the sheet:
  //   DIN: initial=0xaaaaaa
endmodule

module SDMAC_MAIN (
  input  in_1,
  input  in_2,
  input  in_3,
  input  [31:0] in_4,
  input  in_5,
  input  in_6,
  input  in_7,
  input  in_8,
  input  in_9,
  input  in_10,
  input  in_11,
  input  in_12,
  output out_13,
  output out_14,
  output [31:0] out_15
);

  FIFO fifo_1 (
    .INC_FIFO(in_1), .DEC_FIFO(in_2), .INC_NI(in_3), .ID(in_4), .INC_NO(in_5), .INC_BO(in_6), .nRST(1'b1),
    .MID25(in_7), .ACR_WR(in_8), .h_0C(in_9), .LHW(in_10), .nLB(in_11), .LLW(in_12), .FIFO_EMPTY(out_13),
    .FIFO_FULL(out_14), .OD(out_15));  // open: BOEQ0, BOEQ3
endmodule

module FIFO_FullEmptyCounter (
  input  INC_FIFO,
  input  nRST_FIFO,
  input  DEC_FIFO,
  output FIFO_EMPTY,
  output FIFO_FULL
);

  wire and_1_out, and_2_out, d_ff_1_q, d_ff_1_qn, d_ff_2_qn, d_ff_3_q, d_ff_3_qn, d_ff_4_qn, d_ff_5_q,
       d_ff_5_qn, d_ff_6_qn, d_ff_7_q, d_ff_7_qn, d_ff_8_qn, d_ff_9_q, d_ff_9_qn, d_ff_10_qn, d_ff_11_q,
       d_ff_11_qn, d_ff_12_qn, d_ff_13_qn, d_ff_14_q, d_ff_14_qn, d_ff_15_q, d_ff_16_qn, d_ff_17_qn,
       nand_1_out, nand_2_out, nand_3_out, nand_4_out, nand_5_out, nand_6_out, nand_7_out, nand_8_out,
       nand_9_out, nor_1_out, nor_2_out, nor_3_out, not_1_out, not_2_out, not_3_out, not_4_out, not_5_out,
       not_6_out, not_7_out, not_8_out, not_9_out, not_10_out, not_11_out, not_12_out, not_13_out,
       not_14_out, not_15_out, not_16_out, not_17_out, not_18_out, not_19_out, not_20_out, not_21_out,
       not_22_out, not_23_out, not_24_out, not_25_out, not_26_out, or_1_out;

  not not_1 (not_1_out, INC_FIFO);
  nand nand_1 (nand_1_out, not_4_out, not_7_out);
  not not_2 (not_2_out, not_11_out);
  not not_3 (not_3_out, DEC_FIFO);
  not not_4 (not_4_out, not_5_out);
  not not_5 (not_5_out, or_1_out);
  not not_6 (not_6_out, not_1_out);
  and and_1 (and_1_out, nand_1_out, not_2_out);
  not not_7 (not_7_out, not_3_out);
  or or_1 (or_1_out, d_ff_1_q, d_ff_3_q, d_ff_5_q, d_ff_7_q, d_ff_9_q, d_ff_11_q, d_ff_14_q, d_ff_15_q);
  D_Flip_Flop d_ff_1 (.D(1'b1), .clk(not_6_out), .Q(d_ff_1_q), .Qn(d_ff_1_qn), .reset(not_8_out));  // open: preset
  not not_8 (not_8_out, and_1_out);
  D_Flip_Flop d_ff_2 (.D(nand_3_out), .clk(not_7_out), .Qn(d_ff_2_qn), .reset(not_11_out));  // open: Q, preset
  D_Flip_Flop d_ff_3 (
    .D(nand_2_out), .clk(not_6_out), .Q(d_ff_3_q), .Qn(d_ff_3_qn), .reset(not_8_out));  // open: preset
  nand nand_2 (nand_2_out, d_ff_1_qn, d_ff_2_qn);
  D_Flip_Flop d_ff_4 (.D(nand_4_out), .clk(not_7_out), .Qn(d_ff_4_qn), .reset(not_11_out));  // open: Q, preset
  nand nand_3 (nand_3_out, d_ff_3_qn, d_ff_4_qn);
  D_Flip_Flop d_ff_5 (
    .D(nand_3_out), .clk(not_6_out), .Q(d_ff_5_q), .Qn(d_ff_5_qn), .reset(not_8_out));  // open: preset
  D_Flip_Flop d_ff_6 (.D(nand_5_out), .clk(not_7_out), .Qn(d_ff_6_qn), .reset(not_11_out));  // open: Q, preset
  nand nand_4 (nand_4_out, d_ff_5_qn, d_ff_6_qn);
  D_Flip_Flop d_ff_7 (
    .D(nand_4_out), .clk(not_6_out), .Q(d_ff_7_q), .Qn(d_ff_7_qn), .reset(not_8_out));  // open: preset
  D_Flip_Flop d_ff_8 (.D(nand_6_out), .clk(not_7_out), .Qn(d_ff_8_qn), .reset(not_11_out));  // open: Q, preset
  D_Flip_Flop d_ff_9 (
    .D(nand_5_out), .clk(not_6_out), .Q(d_ff_9_q), .Qn(d_ff_9_qn), .reset(not_8_out));  // open: preset
  nand nand_5 (nand_5_out, d_ff_7_qn, d_ff_8_qn);
  D_Flip_Flop d_ff_10 (.D(nand_7_out), .clk(not_7_out), .Qn(d_ff_10_qn), .reset(not_11_out));  // open: Q, preset
  D_Flip_Flop d_ff_11 (
    .D(nand_6_out), .clk(not_6_out), .Q(d_ff_11_q), .Qn(d_ff_11_qn), .reset(not_8_out));  // open: preset
  nand nand_6 (nand_6_out, d_ff_9_qn, d_ff_10_qn);
  D_Flip_Flop d_ff_12 (.D(nand_9_out), .clk(not_7_out), .Qn(d_ff_12_qn), .reset(not_11_out));  // open: Q, preset
  nand nand_7 (nand_7_out, d_ff_11_qn, d_ff_12_qn);
  D_Flip_Flop d_ff_13 (.D(and_2_out), .clk(not_7_out), .Qn(d_ff_13_qn), .reset(not_11_out));  // open: Q, preset
  D_Flip_Flop d_ff_14 (
    .D(nand_7_out), .clk(not_6_out), .Q(d_ff_14_q), .Qn(d_ff_14_qn), .reset(not_8_out));  // open: preset
  not not_9 (not_9_out, not_10_out);
  not not_10 (not_10_out, not_12_out);
  nand nand_8 (nand_8_out, not_9_out, not_17_out, INC_FIFO);
  nand nand_9 (nand_9_out, d_ff_14_qn, d_ff_13_qn);
  not not_11 (not_11_out, not_17_out);
  not not_12 (not_12_out, not_13_out);
  not not_13 (not_13_out, not_15_out);
  D_Flip_Flop d_ff_15 (.D(nand_9_out), .clk(not_6_out), .Q(d_ff_15_q), .reset(not_8_out));  // open: Qn, preset
  D_Flip_Flop d_ff_16 (
    .D(nand_9_out), .clk(INC_FIFO), .Q(FIFO_FULL), .Qn(d_ff_16_qn), .reset(not_14_out));  // open: preset
  not not_14 (not_14_out, nor_1_out);
  not not_15 (not_15_out, not_16_out);
  not not_16 (not_16_out, not_18_out);
  and and_2 (and_2_out, d_ff_15_q, d_ff_15_q);
  not not_17 (not_17_out, not_19_out);
  nor nor_1 (nor_1_out, not_19_out, nor_3_out);
  not not_18 (not_18_out, d_ff_17_qn);
  nor nor_2 (nor_2_out, 1'b0, nand_3_out, nand_4_out, nand_5_out, nand_6_out, nand_7_out, nand_9_out, d_ff_15_q);
  not not_19 (not_19_out, nRST_FIFO);
  nor nor_3 (nor_3_out, not_3_out, not_20_out);
  not not_20 (not_20_out, not_21_out);
  not not_21 (not_21_out, not_23_out);
  D_Flip_Flop d_ff_17 (
    .D(nor_2_out), .clk(DEC_FIFO), .Q(FIFO_EMPTY), .Qn(d_ff_17_qn), .preset(not_19_out), .reset(not_22_out));
  not not_22 (not_22_out, nand_8_out);
  not not_23 (not_23_out, not_24_out);
  not not_24 (not_24_out, not_25_out);
  not not_25 (not_25_out, not_26_out);
  not not_26 (not_26_out, d_ff_16_qn);
endmodule

module FIFO_TEST (
  input  [31:0] in_1
);

  wire and_1_out, and_2_out, clock_1_out, d_ff_1_q, d_ff_1_qn, fifo_1_fifo_empty, fifo_1_fifo_full,
       not_1_out, por_1_out;
  wire [31:0] fifo_1_od;

  D_Flip_Flop d_ff_1 (
    .Q(d_ff_1_q), .Qn(d_ff_1_qn), .preset(fifo_1_fifo_empty), .reset(fifo_1_fifo_full));  // open: D, clk
  Clock clock_1 (.out(clock_1_out));
  POR #(.PorHighDuration(1)) por_1 (.out(por_1_out));
  and and_1 (and_1_out, clock_1_out, d_ff_1_qn);
  not not_1 (not_1_out, por_1_out);
  and and_2 (and_2_out, clock_1_out, d_ff_1_q);
  FIFO fifo_1 (
    .INC_FIFO(and_2_out), .DEC_FIFO(and_1_out), .INC_NI(and_2_out), .ID(in_1), .INC_NO(and_1_out),
    .nRST(not_1_out), .LHW(and_2_out), .nLB(1'b1), .LLW(and_2_out), .FIFO_EMPTY(fifo_1_fifo_empty),
    .FIFO_FULL(fifo_1_fifo_full), .OD(fifo_1_od));  // open: INC_BO, MID25, ACR_WR, h_0C, BOEQ0, BOEQ3
  // Probe on fifo_1_od
endmodule

module DATAPATH_OUTPUT (
  input  nDOEL,
  input  [31:0] M_OD,
  input  BRIDGEOUT,
  input  F2CPUL,
  input  LOD1_F2CPU,
  input  [31:0] OD,
  input  LOD2_F2CPU,
  input  F2CPUH,
  input  nDOEH,
  output [31:0] D
);

  wire not_1_out, not_2_out;
  wire [15:0] register_1_q, register_2_q;

  not not_1 (not_1_out, nDOEL);
  Register #(.width(16)) register_1 (.D(OD[15:0]), .en(LOD1_F2CPU), .clk(LOD1_F2CPU), .Q(register_1_q), .clr(1'b0));
  Register #(.width(16)) register_2 (.D(OD[31:16]), .en(LOD2_F2CPU), .clk(LOD2_F2CPU), .Q(register_2_q), .clr(1'b0));
  not not_2 (not_2_out, nDOEH);
  assign M_OD[31:16] = BRIDGEOUT ? register_1_q : 16'bz;  // Controlled_Buffer controlled_buffer_1
  assign M_OD[15:0] = F2CPUL ? register_1_q : 16'bz;  // Controlled_Buffer controlled_buffer_2
  assign M_OD[31:16] = F2CPUH ? register_2_q : 16'bz;  // Controlled_Buffer controlled_buffer_3
  assign D[15:0] = not_1_out ? M_OD[15:0] : 16'bz;  // Controlled_Buffer controlled_buffer_4
  assign D[31:16] = not_2_out ? M_OD[31:16] : 16'bz;  // Controlled_Buffer controlled_buffer_5
endmodule

module DATAPATH_INPUT (
  input  bBRIDGEIN,
  input  BnDS_O,
  input  bDIEH,
  input  [31:0] D,
  input  bDIEL,
  output [31:0] ID,
  output [31:0] MID
);

  wire [15:0] register_1_q;

  assign MID[15:0] = D[15:0];  // Buffer buffer_1, 16 bits wide
  assign MID[31:16] = D[31:16];  // Buffer buffer_2, 16 bits wide
  Register #(.width(16)) register_1 (.D(MID[15:0]), .en(BnDS_O), .clk(BnDS_O), .Q(register_1_q), .clr(1'b0));
  assign ID[15:0] = bDIEH ? MID[15:0] : 16'bz;  // Controlled_Buffer controlled_buffer_1
  assign ID[31:16] = bDIEL ? MID[31:16] : 16'bz;  // Controlled_Buffer controlled_buffer_2
  assign ID[31:16] = bBRIDGEIN ? register_1_q : 16'bz;  // Controlled_Buffer controlled_buffer_3
endmodule

module DATAPATH (
);

  DATAPATH_INPUT datapath_input_1 ();  // open: bBRIDGEIN, BnDS_O, bDIEH, D, bDIEL, ID, MID
  DATAPATH_OUTPUT datapath_output_1 ();  // open: nDOEL, M_OD, BRIDGEOUT, F2CPUL, LOD1_F2CPU, OD, LOD2_F2CPU, F2CPUH, nDOEH, D
endmodule
